// Logisim project Circuito Calculadora.circ as structural Verilog: 4 circuits, main circuit main
// q
module main (
  input  in_1,
  input  in_2,
  input  in_3,
  input  in_4,
  input  in_5,
  input  in_6,
  input  in_7,
  input  in_8,
  input  in_9,
  input  in_10,
  input  in_11,
  input  in_12,
  input  in_13,
  input  in_14,
  input  in_15,
  input  in_16,
  input  in_17,
  input  in_18,
  input  in_19,
  input  in_20,
  input  in_21,
  input  in_22,
  input  in_23,
  input  in_24,
  input  in_25,
  output out_26,
  output out_27,
  output out_28,
  output out_29,
  output out_30,
  output out_31,
  output out_32,
  output out_33,
  output out_34,
  output out_35,
  output out_36,
  output out_37
);

  wire sumador_completo_1_s__carreo, sumador_completo_2_s__carreo, sumador_completo_3_s__carreo,
       sumador_completo_4_s__carreo, sumador_completo_5_s__carreo, sumador_completo_6_s__carreo,
       sumador_completo_7_s__carreo, sumador_completo_8_s__carreo, sumador_completo_9_s__carreo,
       sumador_completo_10_s__carreo, sumador_completo_11_s__carreo, sumador_completo_12_s__carreo;

  sumador_completo sumador_completo_1 (
    .a(in_1), .b(in_2), .c(in_3), .s__carreo(sumador_completo_1_s__carreo), .r__resultado(out_26));
  sumador_completo sumador_completo_2 (
    .a(in_4), .b(in_5), .c(sumador_completo_1_s__carreo), .s__carreo(sumador_completo_2_s__carreo),
    .r__resultado(out_27));
  sumador_completo sumador_completo_3 (
    .a(in_6), .b(in_7), .c(sumador_completo_2_s__carreo), .s__carreo(sumador_completo_3_s__carreo),
    .r__resultado(out_28));
  sumador_completo sumador_completo_4 (
    .a(in_8), .b(in_9), .c(sumador_completo_3_s__carreo), .s__carreo(sumador_completo_4_s__carreo),
    .r__resultado(out_29));
  sumador_completo sumador_completo_5 (
    .a(in_10), .b(in_11), .c(sumador_completo_4_s__carreo), .s__carreo(sumador_completo_5_s__carreo),
    .r__resultado(out_30));
  sumador_completo sumador_completo_6 (
    .a(in_12), .b(in_13), .c(sumador_completo_5_s__carreo), .s__carreo(sumador_completo_6_s__carreo),
    .r__resultado(out_31));
  sumador_completo sumador_completo_7 (
    .a(in_14), .b(in_15), .c(sumador_completo_6_s__carreo), .s__carreo(sumador_completo_7_s__carreo),
    .r__resultado(out_32));
  sumador_completo Sumador_completo_de_dos_bits ();  // open: a, b, c, s__carreo, r__resultado
  sumador_completo sumador_completo_8 (
    .a(in_16), .b(in_17), .c(sumador_completo_7_s__carreo), .s__carreo(sumador_completo_8_s__carreo),
    .r__resultado(out_33));
  sumador_completo sumador_completo_9 (
    .a(in_18), .b(in_19), .c(sumador_completo_8_s__carreo), .s__carreo(sumador_completo_9_s__carreo),
    .r__resultado(out_34));
  sumador_completo sumador_completo_10 (
    .a(in_20), .b(in_21), .c(sumador_completo_9_s__carreo), .s__carreo(sumador_completo_10_s__carreo),
    .r__resultado(out_35));
  sumador_completo sumador_completo_11 (
    .a(in_22), .b(in_23), .c(sumador_completo_10_s__carreo), .s__carreo(sumador_completo_11_s__carreo),
    .r__resultado(out_36));
  sumador_completo sumador_completo_12 (
    .a(in_24), .b(in_25), .c(sumador_completo_11_s__carreo), .s__carreo(sumador_completo_12_s__carreo),
    .r__resultado(out_37));
  LED Overflow (.in(sumador_completo_12_s__carreo));

  // Notes on the sheet:
  //   carreo 
  //   carreo 
  //   resultado
endmodule

// CSC
module sumador_completo (
  input  a,
  input  b,
  input  c,
  output s__carreo,
  output r__resultado
);

  wire a_b_c_out, a_b_c_prime_out, a_b_prime_c_out, a_b_prime_c_prime_out, a_prime_b_c_out,
       a_prime_b_c_prime_out, a_prime_b_prime_c_out, not_1_out, not_2_out, not_3_out;

  not not_1 (not_1_out, a);
  not not_2 (not_2_out, b);
  not not_3 (not_3_out, c);
  or a_b_c_prime (a_b_c_prime_out, a, b, not_3_out);
  or a_prime_b_c (a_prime_b_c_out, not_1_out, b, c);
  or a_b_prime_c (a_b_prime_c_out, a, not_2_out, c);
  or a_b_c (a_b_c_out, a, b, c);
  or a_prime_b_c_prime (a_prime_b_c_prime_out, not_1_out, b, not_3_out);
  or a_b_prime_c_prime (a_b_prime_c_prime_out, a, not_2_out, not_3_out);
  or a_prime_b_prime_c (a_prime_b_prime_c_out, not_1_out, not_2_out, c);
  and and_1 (s__carreo, a_b_c_prime_out, a_prime_b_c_out, a_b_prime_c_out, a_b_c_out);
  and and_2 (r__resultado, a_b_c_out, a_prime_b_c_prime_out, a_b_prime_c_prime_out, a_prime_b_prime_c_out);
endmodule

module complemento_a_base_2__12_bits (
  input  in_1,
  input  in_2,
  input  in_3,
  input  in_4,
  input  in_5,
  input  in_6,
  input  in_7,
  input  in_8,
  input  in_9,
  input  in_10,
  input  in_11,
  input  in_12,
  output out_13,
  output out_14,
  output out_15,
  output out_16,
  output out_17,
  output out_18,
  output out_19,
  output out_20,
  output out_21,
  output out_22,
  output out_23,
  output out_24
);

  wire not_1_out, not_2_out, not_3_out, not_4_out, not_5_out, not_6_out, not_7_out, not_8_out, not_9_out,
       not_10_out, not_11_out, not_12_out, sumador_completo_1_s__carreo, sumador_completo_2_s__carreo,
       sumador_completo_3_s__carreo, sumador_completo_4_s__carreo, sumador_completo_5_s__carreo,
       sumador_completo_6_s__carreo, sumador_completo_7_s__carreo, sumador_completo_8_s__carreo,
       sumador_completo_9_s__carreo, sumador_completo_10_s__carreo, sumador_completo_11_s__carreo,
       sumador_completo_12_s__carreo;

  not not_1 (not_1_out, in_1);
  not not_2 (not_2_out, in_2);
  not not_3 (not_3_out, in_3);
  not not_4 (not_4_out, in_4);
  not not_5 (not_5_out, in_5);
  not not_6 (not_6_out, in_6);
  not not_7 (not_7_out, in_7);
  not not_8 (not_8_out, in_8);
  not not_9 (not_9_out, in_9);
  not not_10 (not_10_out, in_10);
  not not_11 (not_11_out, in_11);
  not not_12 (not_12_out, in_12);
  sumador_completo sumador_completo_1 (
    .a(not_1_out), .b(1'b1), .c(1'b0), .s__carreo(sumador_completo_1_s__carreo), .r__resultado(out_13));
  sumador_completo sumador_completo_2 (
    .a(not_2_out), .b(1'b0), .c(sumador_completo_1_s__carreo), .s__carreo(sumador_completo_2_s__carreo),
    .r__resultado(out_14));
  sumador_completo sumador_completo_3 (
    .a(not_3_out), .b(1'b0), .c(sumador_completo_2_s__carreo), .s__carreo(sumador_completo_3_s__carreo),
    .r__resultado(out_15));
  sumador_completo sumador_completo_4 (
    .a(not_4_out), .b(1'b0), .c(sumador_completo_3_s__carreo), .s__carreo(sumador_completo_4_s__carreo),
    .r__resultado(out_16));
  sumador_completo sumador_completo_5 (
    .a(not_5_out), .b(1'b0), .c(sumador_completo_4_s__carreo), .s__carreo(sumador_completo_5_s__carreo),
    .r__resultado(out_17));
  sumador_completo sumador_completo_6 (
    .a(not_6_out), .b(1'b0), .c(sumador_completo_5_s__carreo), .s__carreo(sumador_completo_6_s__carreo),
    .r__resultado(out_18));
  sumador_completo sumador_completo_7 (
    .a(not_7_out), .b(1'b0), .c(sumador_completo_6_s__carreo), .s__carreo(sumador_completo_7_s__carreo),
    .r__resultado(out_19));
  sumador_completo sumador_completo_8 (
    .a(not_8_out), .b(1'b0), .c(sumador_completo_7_s__carreo), .s__carreo(sumador_completo_8_s__carreo),
    .r__resultado(out_20));
  sumador_completo Sumador_completo_de_dos_bits ();  // open: a, b, c, s__carreo, r__resultado
  sumador_completo sumador_completo_9 (
    .a(not_9_out), .b(1'b0), .c(sumador_completo_8_s__carreo), .s__carreo(sumador_completo_9_s__carreo),
    .r__resultado(out_21));
  sumador_completo sumador_completo_10 (
    .a(not_10_out), .b(1'b0), .c(sumador_completo_9_s__carreo), .s__carreo(sumador_completo_10_s__carreo),
    .r__resultado(out_22));
  sumador_completo sumador_completo_11 (
    .a(not_11_out), .b(1'b0), .c(sumador_completo_10_s__carreo), .s__carreo(sumador_completo_11_s__carreo),
    .r__resultado(out_23));
  sumador_completo sumador_completo_12 (
    .a(not_12_out), .b(1'b0), .c(sumador_completo_11_s__carreo), .s__carreo(sumador_completo_12_s__carreo),
    .r__resultado(out_24));
  LED Overflow (.in(sumador_completo_12_s__carreo));

  // Notes on the sheet:
  //   carreo 
  //   carreo 
  //   resultado
endmodule

module sumador_de_12_bits (
  input  [11:0] entrada_A,
  input  [11:0] entrada_B,
  output [11:0] out_3
);

  wire sumador_completo_1_r__resultado, sumador_completo_1_s__carreo, sumador_completo_2_r__resultado,
       sumador_completo_2_s__carreo, sumador_completo_3_r__resultado, sumador_completo_3_s__carreo,
       sumador_completo_4_r__resultado, sumador_completo_4_s__carreo, sumador_completo_5_r__resultado,
       sumador_completo_5_s__carreo, sumador_completo_6_r__resultado, sumador_completo_6_s__carreo,
       sumador_completo_7_r__resultado, sumador_completo_7_s__carreo, sumador_completo_8_r__resultado,
       sumador_completo_8_s__carreo, sumador_completo_9_r__resultado, sumador_completo_9_s__carreo,
       sumador_completo_10_r__resultado, sumador_completo_10_s__carreo, sumador_completo_11_r__resultado,
       sumador_completo_11_s__carreo, sumador_completo_12_r__resultado, sumador_completo_12_s__carreo;

  sumador_completo sumador_completo_1 (
    .a(entrada_A[0]), .b(entrada_B[0]), .c(1'b0), .s__carreo(sumador_completo_1_s__carreo),
    .r__resultado(sumador_completo_1_r__resultado));
  sumador_completo sumador_completo_2 (
    .a(entrada_A[1]), .b(entrada_B[1]), .c(sumador_completo_1_s__carreo),
    .s__carreo(sumador_completo_2_s__carreo), .r__resultado(sumador_completo_2_r__resultado));
  sumador_completo sumador_completo_3 (
    .a(entrada_A[2]), .b(entrada_B[2]), .c(sumador_completo_2_s__carreo),
    .s__carreo(sumador_completo_3_s__carreo), .r__resultado(sumador_completo_3_r__resultado));
  sumador_completo sumador_completo_4 (
    .a(entrada_A[3]), .b(entrada_B[3]), .c(sumador_completo_3_s__carreo),
    .s__carreo(sumador_completo_4_s__carreo), .r__resultado(sumador_completo_4_r__resultado));
  sumador_completo sumador_completo_5 (
    .a(entrada_A[4]), .b(entrada_B[4]), .c(sumador_completo_4_s__carreo),
    .s__carreo(sumador_completo_5_s__carreo), .r__resultado(sumador_completo_5_r__resultado));
  sumador_completo Sumador_completo_de_dos_bits ();  // open: a, b, c, s__carreo, r__resultado
  sumador_completo sumador_completo_6 (
    .a(entrada_A[5]), .b(entrada_B[5]), .c(sumador_completo_5_s__carreo),
    .s__carreo(sumador_completo_6_s__carreo), .r__resultado(sumador_completo_6_r__resultado));
  sumador_completo sumador_completo_7 (
    .a(entrada_A[6]), .b(entrada_B[6]), .c(sumador_completo_6_s__carreo),
    .s__carreo(sumador_completo_7_s__carreo), .r__resultado(sumador_completo_7_r__resultado));
  sumador_completo sumador_completo_8 (
    .a(entrada_A[7]), .b(entrada_B[7]), .c(sumador_completo_7_s__carreo),
    .s__carreo(sumador_completo_8_s__carreo), .r__resultado(sumador_completo_8_r__resultado));
  sumador_completo sumador_completo_9 (
    .a(entrada_A[8]), .b(entrada_B[8]), .c(sumador_completo_8_s__carreo),
    .s__carreo(sumador_completo_9_s__carreo), .r__resultado(sumador_completo_9_r__resultado));
  sumador_completo sumador_completo_10 (
    .a(entrada_A[9]), .b(entrada_B[9]), .c(sumador_completo_9_s__carreo),
    .s__carreo(sumador_completo_10_s__carreo), .r__resultado(sumador_completo_10_r__resultado));
  sumador_completo sumador_completo_11 (
    .a(entrada_A[10]), .b(entrada_B[10]), .c(sumador_completo_10_s__carreo),
    .s__carreo(sumador_completo_11_s__carreo), .r__resultado(sumador_completo_11_r__resultado));
  sumador_completo sumador_completo_12 (
    .a(entrada_A[11]), .b(entrada_B[11]), .c(sumador_completo_11_s__carreo),
    .s__carreo(sumador_completo_12_s__carreo), .r__resultado(sumador_completo_12_r__resultado));
  LED Overflow (.in(sumador_completo_12_s__carreo));
  // Buffer buffer_1 has open pins: in=open, out=out_3

  // Notes on the sheet:
  //   carreo 
  //   carreo 
  //   resultado
endmodule
